// Logisim project 1bit_full_comparator.circ as structural Verilog: 1 circuit, main circuit main
module main (
  input  A,
  input  B,
  output A_greater,
  output B_greater,
  output A_equal_B
);

  wire not_1_out, not_2_out;

  not not_1 (not_1_out, B);
  not not_2 (not_2_out, A);
  and and_1 (A_greater, A, not_1_out);
  and and_2 (B_greater, not_2_out, B);
  xnor xnor_1 (A_equal_B, A, B);
endmodule
