// Logisim project adder.circ as structural Verilog: 6 circuits, main circuit byte_adder_subtractor
module half_adder (
  input  A,
  input  B,
  output S,
  output Cout
);

  and and_1 (Cout, B, A);
  xor xor_1 (S, A, B);
endmodule

module full_adder (
  input  A,
  input  B,
  input  Cin,
  output S,
  output Cout
);

  wire and_1_out, and_2_out, xor_1_out;

  xor xor_1 (xor_1_out, A, B);
  and and_1 (and_1_out, A, B);
  xor xor_2 (S, xor_1_out, Cin);
  and and_2 (and_2_out, xor_1_out, Cin);
  or or_1 (Cout, and_2_out, and_1_out);
endmodule

module four_bit_adder (
  input  in_1,
  input  in_2,
  input  B0,
  input  A0,
  input  D1,
  input  C1,
  input  B1,
  input  A1,
  input  in_9,
  output out_10,
  output Cout,
  output S3,
  output S2,
  output S1,
  output S0
);

  wire full_adder_3_cout, full_adder_4_cout;

  full_adder full_adder_1 (.A(in_1), .B(D1), .Cin(out_10), .S(S3), .Cout(Cout));
  full_adder full_adder_2 (.A(in_2), .B(C1), .Cin(full_adder_3_cout), .S(S2), .Cout(out_10));
  full_adder full_adder_3 (.A(B0), .B(B1), .Cin(full_adder_4_cout), .S(S1), .Cout(full_adder_3_cout));
  full_adder full_adder_4 (.A(A0), .B(A1), .Cin(in_9), .S(S0), .Cout(full_adder_4_cout));
endmodule

module operation_select (
  input  in_1,
  input  in_2,
  input  in_3,
  input  in_4,
  input  in_5,
  output out_6,
  output out_7,
  output out_8,
  output out_9,
  output out_10,
  output out_11
);

  xor xor_1 (out_8, in_1, in_5);
  xor xor_2 (out_9, in_2, in_5);
  xor xor_3 (out_10, in_3, in_5);
  xor xor_4 (out_11, in_4, in_5);

  assign out_6 = in_5;
  assign out_7 = in_5;
endmodule

module overflow_flag (
  input  in_1,
  input  in_2,
  output out_3
);

  xor xor_1 (out_3, in_1, in_2);
endmodule

module byte_adder_subtractor (
  input  _7,
  input  _6,
  input  _5,
  input  _4,
  input  _3,
  input  _2,
  input  _1,
  input  _0,
  input  B,
  input  in_10,
  input  in_11,
  input  in_12,
  input  in_13,
  input  in_14,
  input  in_15,
  input  in_16,
  input  in_17,
  output out_18,
  output out_19,
  output out_20,
  output out_21,
  output out_22,
  output out_23,
  output out_24,
  output out_25,
  output out_26,
  output out_27
);

  wire four_bit_adder_1_out_10, four_bit_adder_2_cout, operation_select_1_out_8, operation_select_1_out_9,
       operation_select_1_out_10, operation_select_1_out_11, operation_select_2_out_6,
       operation_select_2_out_7, operation_select_2_out_8, operation_select_2_out_9,
       operation_select_2_out_10, operation_select_2_out_11;

  overflow_flag overflow_flag_1 (.in_1(four_bit_adder_1_out_10), .in_2(out_18), .out_3(out_19));
  operation_select operation_select_1 (
    .in_1(B), .in_2(in_10), .in_3(in_11), .in_4(in_12), .in_5(operation_select_2_out_6),
    .out_8(operation_select_1_out_8), .out_9(operation_select_1_out_9), .out_10(operation_select_1_out_10),
    .out_11(operation_select_1_out_11));  // open: out_6, out_7
  four_bit_adder four_bit_adder_1 (
    .in_1(_7), .D1(operation_select_1_out_8), .in_2(_6), .C1(operation_select_1_out_9), .B0(_5),
    .B1(operation_select_1_out_10), .A0(_4), .A1(operation_select_1_out_11), .in_9(four_bit_adder_2_cout),
    .out_10(four_bit_adder_1_out_10), .S3(out_20), .S2(out_21), .S1(out_22), .S0(out_23), .Cout(out_18));
  operation_select operation_select_2 (
    .in_1(in_13), .in_2(in_14), .in_3(in_15), .in_4(in_16), .in_5(in_17), .out_6(operation_select_2_out_6),
    .out_8(operation_select_2_out_8), .out_9(operation_select_2_out_9), .out_10(operation_select_2_out_10),
    .out_11(operation_select_2_out_11), .out_7(operation_select_2_out_7));
  four_bit_adder four_bit_adder_2 (
    .in_1(_3), .D1(operation_select_2_out_8), .in_2(_2), .C1(operation_select_2_out_9), .B0(_1),
    .B1(operation_select_2_out_10), .A0(_0), .A1(operation_select_2_out_11), .in_9(operation_select_2_out_7),
    .S3(out_24), .S2(out_25), .S1(out_26), .S0(out_27), .Cout(four_bit_adder_2_cout));  // open: out_10

  // Notes on the sheet:
  //   A
endmodule
