// Logisim project half_subtractor.circ as structural Verilog: 1 circuit, main circuit main
module main (
  input  in_1,
  input  in_2,
  output out_3,
  output out_4
);

  and and_1 (out_4, in_2, ~in_1);  // AND_Gate
  xor xor_1 (out_3, in_1, in_2);
endmodule
