// Logisim project half_adder.circ as structural Verilog
module exclusive_or (
  input  in_1,
  input  in_2,
  output out_3,
  output out_4
);

  wire and_2_out, and_3_out, not_1_out, not_2_out;

  not not_1 (not_1_out, in_1);
  not not_2 (not_2_out, in_2);
  and and_1 (out_4, in_2, in_1);
  and and_2 (and_2_out, not_1_out, in_2);
  and and_3 (and_3_out, in_1, not_2_out);
  or or_1 (out_3, and_2_out, and_3_out);
endmodule
