// Logisim project SAP1.circ as structural Verilog: 2 circuits, main circuit Main
module Add_Sub (
  input  EU,
  input  A7,
  input  A6,
  input  A5,
  input  A4,
  input  A3,
  input  A2,
  input  A1,
  input  A0,
  input  B7,
  input  B6,
  input  B5,
  input  B4,
  input  B3,
  input  B2,
  input  B1,
  input  B0,
  input  SU,
  output [7:0] O
);

  wire and_1_out, and_2_out, and_3_out, and_4_out, and_5_out, and_6_out, and_7_out, and_8_out, and_9_out,
       and_10_out, and_11_out, and_12_out, and_13_out, and_14_out, and_15_out, and_16_out, or_1_out,
       or_2_out, or_3_out, or_4_out, or_5_out, or_6_out, or_7_out, or_8_out, xor_2_out, xor_3_out, xor_5_out,
       xor_6_out, xor_8_out, xor_9_out, xor_11_out, xor_12_out, xor_14_out, xor_15_out, xor_17_out,
       xor_18_out, xor_20_out, xor_21_out, xor_23_out, xor_24_out;
  wire [7:0] xor_22_out;

  assign O = EU ? xor_22_out : 8'bz;  // Controlled_Buffer controlled_buffer_1
  or or_1 (or_1_out, and_2_out, and_1_out);
  xor xor_1 (xor_22_out[7], xor_2_out, or_2_out);
  and and_1 (and_1_out, xor_2_out, or_2_out);
  xor xor_2 (xor_2_out, A7, xor_3_out);
  and and_2 (and_2_out, A7, xor_3_out);
  xor xor_3 (xor_3_out, B7, SU);
  or or_2 (or_2_out, and_4_out, and_3_out);
  xor xor_4 (xor_22_out[6], xor_6_out, or_3_out);
  and and_3 (and_3_out, xor_6_out, or_3_out);
  xor xor_5 (xor_5_out, B6, SU);
  xor xor_6 (xor_6_out, A6, xor_5_out);
  and and_4 (and_4_out, A6, xor_5_out);
  or or_3 (or_3_out, and_6_out, and_5_out);
  xor xor_7 (xor_22_out[5], xor_8_out, or_4_out);
  and and_5 (and_5_out, xor_8_out, or_4_out);
  xor xor_8 (xor_8_out, A5, xor_9_out);
  and and_6 (and_6_out, A5, xor_9_out);
  xor xor_9 (xor_9_out, B5, SU);
  or or_4 (or_4_out, and_8_out, and_7_out);
  xor xor_10 (xor_22_out[4], xor_12_out, or_5_out);
  and and_7 (and_7_out, xor_12_out, or_5_out);
  xor xor_11 (xor_11_out, B4, SU);
  xor xor_12 (xor_12_out, A4, xor_11_out);
  and and_8 (and_8_out, A4, xor_11_out);
  or or_5 (or_5_out, and_10_out, and_9_out);
  xor xor_13 (xor_22_out[3], xor_15_out, or_6_out);
  and and_9 (and_9_out, xor_15_out, or_6_out);
  xor xor_14 (xor_14_out, B3, SU);
  xor xor_15 (xor_15_out, A3, xor_14_out);
  and and_10 (and_10_out, A3, xor_14_out);
  or or_6 (or_6_out, and_12_out, and_11_out);
  xor xor_16 (xor_22_out[2], xor_17_out, or_7_out);
  and and_11 (and_11_out, xor_17_out, or_7_out);
  xor xor_17 (xor_17_out, A2, xor_18_out);
  and and_12 (and_12_out, A2, xor_18_out);
  xor xor_18 (xor_18_out, B2, SU);
  or or_7 (or_7_out, and_14_out, and_13_out);
  xor xor_19 (xor_22_out[1], xor_21_out, or_8_out);
  and and_13 (and_13_out, xor_21_out, or_8_out);
  xor xor_20 (xor_20_out, B1, SU);
  xor xor_21 (xor_21_out, A1, xor_20_out);
  and and_14 (and_14_out, A1, xor_20_out);
  or or_8 (or_8_out, and_16_out, and_15_out);
  xor xor_22 (xor_22_out[0], xor_24_out, SU);
  and and_15 (and_15_out, xor_24_out, SU);
  xor xor_23 (xor_23_out, B0, SU);
  xor xor_24 (xor_24_out, A0, xor_23_out);
  and and_16 (and_16_out, A0, xor_23_out);
endmodule

module Main (
);

  Add_Sub add_sub_1 ();  // open: A6, B6, A5, B5, A4, B4, A3, B3, A2, B2, A1, B1, A0, B0, EU, SU, A7, B7, O
endmodule
