// Logisim project latch.circ as structural Verilog: 3 circuits, main circuit SR_Latch
module SR_Latch (
  input  R,
  input  S,
  output Q,
  output Not_Q
);

  nor nor_1 (Q, R, Not_Q);
  nor nor_2 (Not_Q, Q, S);
endmodule

module Enabled_SR_Latch (
  input  R,
  input  E,
  input  S,
  output Q,
  output Not_Q
);

  wire and_1_out, and_2_out;

  and and_1 (and_1_out, R, E);
  and and_2 (and_2_out, E, S);
  nor nor_1 (Q, and_1_out, Not_Q);
  nor nor_2 (Not_Q, Q, and_2_out);
endmodule

module Main (
  input  in_1,
  input  in_2,
  input  in_3,
  input  in_4,
  input  in_5,
  output out_6,
  output out_7,
  output out_8,
  output out_9
);

  SR_Latch sr_latch_1 (.R(in_1), .S(in_4), .Q(out_6), .Not_Q(out_8));
  Enabled_SR_Latch enabled_sr_latch_1 (.R(in_2), .E(in_3), .S(in_5), .Q(out_7), .Not_Q(out_9));
endmodule
